# Fritzing sketch wf_0_0_1 (saved by Fritzing 0.8.7b)
circuit board: 6.88566cm x 5.36311cm
breadboards: 1

parts:
  Part1 = Arduino Uno (Rev3)
  R1 = Resistor [tolerance=±5% resistance=220 package=THT]
  R2 = Resistor [tolerance=±5% resistance=220 package=THT]
  R3 = Resistor [tolerance=±5% resistance=10k package=THT]
  R4 = Resistor [tolerance=±5% resistance=10k package=THT]
  R5 = Resistor [tolerance=±5% resistance=10k package=THT]
  LED2 = LED - 5mm [color="Red (633nm)" package="5 mm [THT]"]
  LED1 = LED - 5mm [color="Green (570nm)" package="5 mm [THT]"]
  R6 = Resistor [tolerance=±5% resistance=10k package=THT]
  R7 = PHOTOCELL [package=photocell-kit]
  T1 = TMP36 Temperature Sensor [package="TO92 [THT]"]
  J1 = male pin header, 4 pins [form="♂ (male)"]

nets:
  N1: Part1.A0, R4.Pin_1, R7.P$1
  N2: Part1.A1, T1.Vout
  N3: Part1.D2, R6.Pin_1, J1.pin1
  N4: Part1.D4, R5.Pin_1, J1.pin3
  N5: Part1.D5_PWM, LED2.cathode
  N6: Part1.D6_PWM, LED1.cathode
  N7: Part1.5V, R7.P$2, T1.+Vs, J1.pin2, J1.pin4
  N8: Part1.GND, R1.Pin_0, R2.Pin_0, R3.Pin_0, R4.Pin_0, R5.Pin_0, R6.Pin_0
  N9: R1.Pin_1, LED2.anode
  N10: R2.Pin_1, LED1.anode
  N11: R3.Pin_1, T1.GND
